# Fritzing sketch Hanimandl_ESP32 (saved by Fritzing 0.9.10b)
circuit board: 8.47cm x 4.8cm
breadboards: 1

parts:
  ws_ssd1327_W/G/O/Y/BLU/BLK/R = screw terminal, 7 pins
  srv/+/- = screw terminal, 3 pins
  +/- = Screw terminal - 2 pins [package=THT]
  hx711 = HX711 Weighing Sensor Module
  Load_E+/E-/A+/A+_or_R/B/W/G = screw terminal, 4 pins
  WS_ESP32-S3-DEV-KIT-N8R8 = female pin header, 22 pins [form="♀ (female)"]
  USB = female pin header, 22 pins [form="♀ (female)"]
  Mom_1/2 = screw terminal, 4 pins
  Switch = screw terminal, 3 pins
  Rot_GND/+/SW/DT/CLK = screw terminal, 5 pins
  + = female alternating pin header, 1 pin [form="♀ (female)"]
  Buzz = female alternating pin header, 1 pin [form="♀ (female)"]

nets:
  N1: ws_ssd1327_W/G/O/Y/BLU/BLK/R.pin1, WS_ESP32-S3-DEV-KIT-N8R8.pin10
  N2: ws_ssd1327_W/G/O/Y/BLU/BLK/R.pin2, WS_ESP32-S3-DEV-KIT-N8R8.pin8
  N3: ws_ssd1327_W/G/O/Y/BLU/BLK/R.pin3, WS_ESP32-S3-DEV-KIT-N8R8.pin7
  N4: ws_ssd1327_W/G/O/Y/BLU/BLK/R.pin4, WS_ESP32-S3-DEV-KIT-N8R8.pin4
  N5: ws_ssd1327_W/G/O/Y/BLU/BLK/R.pin5, WS_ESP32-S3-DEV-KIT-N8R8.pin6
  N6: ws_ssd1327_W/G/O/Y/BLU/BLK/R.pin6, srv/+/-.pin3, +/-.pin2, hx711.GND, WS_ESP32-S3-DEV-KIT-N8R8.pin1
  N7: ws_ssd1327_W/G/O/Y/BLU/BLK/R.pin7, srv/+/-.pin2, +/-.pin1, WS_ESP32-S3-DEV-KIT-N8R8.pin2
  N8: srv/+/-.pin1, USB.pin5
  N9: hx711.VCC, WS_ESP32-S3-DEV-KIT-N8R8.pin21
  N10: hx711.DO/RX, USB.pin14
  N11: hx711.CK/TX, USB.pin13
  N12: hx711.E+, Load_E+/E-/A+/A+_or_R/B/W/G.pin1
  N13: hx711.E-, Load_E+/E-/A+/A+_or_R/B/W/G.pin2
  N14: hx711.A+, Load_E+/E-/A+/A+_or_R/B/W/G.pin3
  N15: hx711.A-, Load_E+/E-/A+/A+_or_R/B/W/G.pin4
  N16: WS_ESP32-S3-DEV-KIT-N8R8.pin12, Switch.pin3
  N17: WS_ESP32-S3-DEV-KIT-N8R8.pin13, Switch.pin2
  N18: WS_ESP32-S3-DEV-KIT-N8R8.pin14, Switch.pin1
  N19: WS_ESP32-S3-DEV-KIT-N8R8.pin15, Mom_1/2.pin4
  N20: WS_ESP32-S3-DEV-KIT-N8R8.pin16, Mom_1/2.pin3
  N21: WS_ESP32-S3-DEV-KIT-N8R8.pin17, Mom_1/2.pin2
  N22: WS_ESP32-S3-DEV-KIT-N8R8.pin18, Mom_1/2.pin1
  N23: WS_ESP32-S3-DEV-KIT-N8R8.pin22, Rot_GND/+/SW/DT/CLK.pin4
  N24: USB.pin6, Rot_GND/+/SW/DT/CLK.pin1
  N25: USB.pin7, Rot_GND/+/SW/DT/CLK.pin2
  N26: USB.pin10, Rot_GND/+/SW/DT/CLK.pin3
  N27: USB.pin18, +.pin1
  N28: USB.pin22, Rot_GND/+/SW/DT/CLK.pin5, Buzz.pin1

notes:
  HANIMANDL, ESP32DEV-Version 1.0
  W.Birkfellner 2023
